// Logisim project 컴퓨터구조.circ as structural Verilog: 7 circuits, main circuit main
module main (
);

  wire clock_1_out, controller_1_out_2, controller_1_out_3, controller_1_out_4, controller_1_out_5,
       controller_1_out_7, controller_1_out_8, controller_1_out_9;
  wire [1:0] controller_1_out_6;
  wire [2:0] alu_control_1_out_3;
  wire [4:0] multiplexer_1_out, splitter_1_out_3, splitter_1_out_4, splitter_1_out_5;
  wire [5:0] splitter_1_out_2;
  wire [15:0] splitter_1_out_6;
  wire [31:0] adder_1_out, adder_2_out, ALU_out_4, multiplexer_2_out, multiplexer_3_out, multiplexer_4_out,
       ram_1_data, ram_2_data, register_1_q, register_2_out_7, register_2_out_8, sign_extend_1_out_2;

  Register_part #(.width(32)) register_1 (
    .D(multiplexer_2_out), .en(1'b1), .Q(register_1_q), .clk(clock_1_out), .clr(1'b0));
  Clock clock_1 (.out(clock_1_out));
  Adder #(.width(32)) adder_1 (.a(register_1_q), .b(32'h1), .out(adder_1_out));  // open: cin, cout
  Splitter splitter_1 (
    .in_1(ram_1_data), .out_2(splitter_1_out_2), .out_3(splitter_1_out_3), .out_4(splitter_1_out_4),
    .out_5(splitter_1_out_5), .out_6(splitter_1_out_6));
  RAM #(.addrWidth(23), .dataWidth(32)) ram_1 (
    .addr(register_1_q[22:0]), .data(ram_1_data));  // open: sel, clk, ld, clr
  Controller controller_1 (
    .in_1(splitter_1_out_2), .out_2(controller_1_out_2), .out_3(controller_1_out_3),
    .out_4(controller_1_out_4), .out_5(controller_1_out_5), .out_6(controller_1_out_6),
    .out_7(controller_1_out_7), .out_8(controller_1_out_8), .out_9(controller_1_out_9));
  Multiplexer #(.width(5)) multiplexer_1 (
    .in0(splitter_1_out_4), .in1(splitter_1_out_5), .out(multiplexer_1_out), .sel(controller_1_out_2));  // open: en
  Sign_Extend sign_extend_1 (.in_1(splitter_1_out_6), .out_2(sign_extend_1_out_2));
  Adder #(.width(32)) adder_2 (.a(adder_1_out), .b(sign_extend_1_out_2), .out(adder_2_out));  // open: cin, cout
  Register register_2 (
    .in_1(splitter_1_out_3), .in_2(splitter_1_out_4), .Write(controller_1_out_9), .in_4(clock_1_out),
    .in_5(multiplexer_1_out), .in_6(multiplexer_4_out), .out_7(register_2_out_7), .out_8(register_2_out_8));
  Multiplexer #(.width(32)) multiplexer_2 (
    .in0(adder_1_out), .in1(adder_2_out), .out(multiplexer_2_out), .sel(controller_1_out_3));  // open: en
  Multiplexer #(.width(32)) multiplexer_3 (
    .in0(register_2_out_8), .in1(sign_extend_1_out_2), .out(multiplexer_3_out), .sel(controller_1_out_8));  // open: en
  ALU_control alu_control_1 (.in_1(controller_1_out_6), .in_2(splitter_1_out_6), .out_3(alu_control_1_out_3));
  simplified_Alu ALU (.in_1(alu_control_1_out_3), .in_2(register_2_out_7), .in_3(multiplexer_3_out), .out_4(ALU_out_4));
  RAM #(.addrWidth(23), .dataWidth(32), .bus("separate")) ram_2 (
    .addr(ALU_out_4[22:0]), .din(register_2_out_8), .data(ram_2_data), .str(controller_1_out_7),
    .clk(clock_1_out), .ld(controller_1_out_4));  // open: sel, clr
  Multiplexer #(.width(32)) multiplexer_4 (
    .in0(ALU_out_4), .in1(ram_2_data), .out(multiplexer_4_out), .sel(controller_1_out_5));  // open: en

  // Notes on the sheet:
  //   Register
  //   Sign Extend
endmodule

module Splitter (
  input  [31:0] in_1,
  output [5:0] out_2,
  output [4:0] out_3,
  output [4:0] out_4,
  output [4:0] out_5,
  output [15:0] out_6
);


  assign out_2 = in_1[31:26];
  assign out_3 = in_1[25:21];
  assign out_4 = in_1[20:16];
  assign out_5 = in_1[15:11];
  assign out_6 = in_1[15:0];
endmodule

module Controller (
  input  [5:0] in_1,
  output out_2,
  output out_3,
  output out_4,
  output out_5,
  output [1:0] out_6,
  output out_7,
  output out_8,
  output out_9
);

  ROM #(.addrWidth(6), .dataWidth(9)) rom_1 (
    .addr(in_1), .data({out_9, out_8, out_7, out_6[0], out_6[1], out_5, out_4, out_3, out_2}));  // open: sel

  // Notes on the sheet:
  //   31-26 
  //   contents of rom_1 (hex, n*v repeats v):
  //   1 11
endmodule

module Register (
  input  [4:0] in_1,
  input  [4:0] in_2,
  input  Write,
  input  in_4,
  input  [4:0] in_5,
  input  [31:0] in_6,
  output [31:0] out_7,
  output [31:0] out_8
);

  wire and_1_out, and_2_out, and_3_out, and_4_out, and_5_out, and_6_out, and_7_out, and_8_out,
       decoder_1_out0, decoder_1_out1, decoder_1_out2, decoder_1_out3, decoder_1_out4, decoder_1_out5,
       decoder_1_out6, decoder_1_out7;
  wire [31:0] register_1_q, register_2_q, register_3_q, register_4_q, register_5_q, register_6_q,
       register_7_q, register_8_q;

  Decoder #(.select(5)) decoder_1 (
    .out0(decoder_1_out0), .out1(decoder_1_out1), .out2(decoder_1_out2), .out3(decoder_1_out3),
    .out4(decoder_1_out4), .out5(decoder_1_out5), .out6(decoder_1_out6), .out7(decoder_1_out7), .sel(in_5));  // open: out8, out9, out10, out11, out12, out13, out14, out15, out16, out17, out18, out19, out20, out21, out22, out23, out24, out25, out26, out27, out28, out29, out30, out31, en
  and and_1 (and_1_out, Write, decoder_1_out0);
  and and_2 (and_2_out, Write, decoder_1_out1);
  and and_3 (and_3_out, Write, decoder_1_out2);
  and and_4 (and_4_out, Write, decoder_1_out3);
  and and_5 (and_5_out, Write, decoder_1_out4);
  and and_6 (and_6_out, Write, decoder_1_out5);
  and and_7 (and_7_out, Write, decoder_1_out6);
  and and_8 (and_8_out, Write, decoder_1_out7);
  Register_part #(.width(32)) register_1 (.D(in_6), .en(and_1_out), .Q(register_1_q), .clk(in_4));  // open: clr
  Register_part #(.width(32)) register_2 (.D(in_6), .en(and_2_out), .Q(register_2_q), .clk(in_4));  // open: clr
  Register_part #(.width(32)) register_3 (.D(in_6), .en(and_3_out), .Q(register_3_q), .clk(in_4));  // open: clr
  Register_part #(.width(32)) register_4 (.D(in_6), .en(and_4_out), .Q(register_4_q), .clk(in_4));  // open: clr
  Register_part #(.width(32)) register_5 (.D(in_6), .en(and_5_out), .Q(register_5_q), .clk(in_4));  // open: clr
  Register_part #(.width(32)) register_6 (.D(in_6), .en(and_6_out), .Q(register_6_q), .clk(in_4));  // open: clr
  Register_part #(.width(32)) register_7 (.D(in_6), .en(and_7_out), .Q(register_7_q), .clk(in_4));  // open: clr
  Register_part #(.width(32)) register_8 (.D(in_6), .en(and_8_out), .Q(register_8_q), .clk(in_4));  // open: clr
  Multiplexer #(.select(5), .width(32)) multiplexer_1 (
    .in0(register_1_q), .in1(register_2_q), .in2(register_3_q), .in3(register_4_q), .in4(register_5_q),
    .in5(register_6_q), .in6(register_7_q), .in7(register_8_q), .out(out_7), .sel(in_1));  // open: in8, in9, in10, in11, in12, in13, in14, in15, in16, in17, in18, in19, in20, in21, in22, in23, in24, in25, in26, in27, in28, in29, in30, in31, en
  Multiplexer #(.select(5), .width(32)) multiplexer_2 (
    .in0(register_1_q), .in1(register_2_q), .in2(register_3_q), .in3(register_4_q), .in4(register_5_q),
    .in5(register_6_q), .in6(register_7_q), .in7(register_8_q), .out(out_8), .sel(in_2));  // open: in8, in9, in10, in11, in12, in13, in14, in15, in16, in17, in18, in19, in20, in21, in22, in23, in24, in25, in26, in27, in28, in29, in30, in31, en
endmodule

module Sign_Extend (
  input  [15:0] in_1,
  output [31:0] out_2
);


  assign out_2 = {{17{in_1[15]}}, in_1[14:0]};
endmodule

module simplified_Alu (
  input  [2:0] in_1,
  input  [31:0] in_2,
  input  [31:0] in_3,
  output [31:0] out_4
);

  wire [31:0] adder_1_out, and_1_out, not_1_out, or_1_out, shifter_1_out, shifter_2_out, subtractor_1_out,
       xor_1_out;

  Adder #(.width(32)) adder_1 (.a(in_3), .b(in_2), .out(adder_1_out));  // open: cin, cout
  Subtractor #(.width(32)) subtractor_1 (.a(in_3), .b(in_2), .out(subtractor_1_out));  // open: bin, bout
  assign or_1_out = in_3 | in_2;  // OR_Gate or_1, 32 bits wide
  assign and_1_out = in_3 & in_2;  // AND_Gate and_1, 32 bits wide
  assign not_1_out = ~in_3;  // NOT_Gate not_1, 32 bits wide
  Shifter #(.width(32)) shifter_1 (.in(in_3), .\dist (5'b00010), .out(shifter_1_out));
  Shifter #(.width(32), .shift("lr")) shifter_2 (.in(in_3), .\dist (5'b00010), .out(shifter_2_out));
  assign xor_1_out = in_3 ^ in_2;  // XOR_Gate xor_1, 32 bits wide
  Multiplexer #(.select(3), .width(32)) multiplexer_1 (
    .in0(in_2), .in1(adder_1_out), .in2(subtractor_1_out), .in3(or_1_out), .in4(and_1_out), .in5(xor_1_out),
    .in6(not_1_out), .in7(shifter_1_out), .out(out_4), .sel(in_1));  // open: en
endmodule

module ALU_control (
  input  [1:0] in_1,
  input  [15:0] in_2,
  output [2:0] out_3
);

  wire and_1_out, not_1_out, not_2_out, or_1_out;

  and and_1 (and_1_out, in_1[1], in_2[1]);
  or or_1 (or_1_out, in_2[3], in_2[0]);
  and and_2 (out_3[0], in_1[1], or_1_out);
  or or_2 (out_3[2], in_1[0], and_1_out);
  not not_1 (not_1_out, in_1[1]);
  not not_2 (not_2_out, in_2[2]);
  or or_3 (out_3[1], not_1_out, not_2_out);
endmodule
